# Fritzing sketch PI_POWER_BOARD (saved by Fritzing 0.9.3b)
circuit board: 9.9cm x 5.8cm
breadboards: 1

parts:
  Raspberry_Pi1 = Raspberry Pi 2
  Q1 = NPN-Transistor [package="TO92 [THT]"]
  R1 = Resistor [tolerance=±5% resistance=1k package=THT]
  PWR_SW = Pushbutton [package="[THT]"]
  PWR_LD = LED - 5mm [color="Red (633nm)" package="5 mm [THT]"]
  R2 = Resistor [tolerance=±5% resistance=220 package=THT]
  D1 = Rectifier Diode [part_number=1N4001 package="300 mil [THT]"]
  FAN = DC Motor
  U1 = LM2596 step down module
  12V = Screw terminal - 2 pins [package=THT]

nets:
  N1: Raspberry_Pi1.GPIO3, PWR_SW.Pin_1, PWR_SW.Pin_2
  N2: Raspberry_Pi1.GPIO4, R1.Pin_0
  GND: Raspberry_Pi1.GND, Q1.E, PWR_SW.Pin_3, PWR_SW.Pin_4, R2.Pin_1, U1.IN-, U1.OUT-, 12V.pin1
  N3: Raspberry_Pi1.GPIO14, PWR_LD.anode
  N4: Raspberry_Pi1.5V, D1.cathode, FAN.pin_1, U1.OUT+
  N5: Q1.B, R1.Pin_1
  N6: Q1.C, D1.anode, FAN.pin_2
  N7: PWR_LD.cathode, R2.Pin_0
  N8: U1.IN+, 12V.pin2

notes:
  +
  -

custom parts:
  LM2596 step down module: LM2596 DC-DC step down power supply module 3 A.
